# Fritzing sketch pysounds_PCB (saved by Fritzing 0.8.0b)
breadboards: 1

parts:
  J1 = FKIT-RIBBON_CONNECTOR [package=fkit-ribbon_connector_03_2mm_l]  # not connected
  R = Resistor [tolerance=±5% resistance=10k package=THT]
  R_2 = Resistor [tolerance=±5% resistance=220 package=THT]
  S2 = Pushbutton [package="[THT]"]
  S3 = Pushbutton [package="[THT]"]
  LED1 = LED - 5mm [color="Red (633nm)" package="5 mm [THT]"]
  LED2 = LED - 5mm [color="Red (633nm)" package="5 mm [THT]"]
  R_3 = Resistor [tolerance=±5% resistance=10k package=THT]
  R_4 = Resistor [tolerance=±5% resistance=10k package=THT]
  S1 = Pushbutton [package="[THT]"]
  R_5 = Resistor [tolerance=±5% resistance=220 package=THT]
  Raspberry_Pi1 = Raspberry Pi  # not connected

nets:
  N1: R.Pin_0, S1.Pin_1, S1.Pin_2
  N2: R.Pin_1, R_3.Pin_1, R_4.Pin_1
  N3: R_2.Pin_0, LED1.cathode
  N4: R_2.Pin_1, S2.Pin_3, S2.Pin_4, S3.Pin_3, S3.Pin_4, S1.Pin_3, S1.Pin_4, R_5.Pin_1
  N5: S2.Pin_1, S2.Pin_2, R_3.Pin_0
  N6: S3.Pin_1, S3.Pin_2, R_4.Pin_0
  N7: LED2.cathode, R_5.Pin_0

notes:
  -
  +
  17
  22
  18
  24
  25
